# Fritzing sketch Nano_ESP32_Cam (saved by Fritzing 0.9.9b)
breadboards: 1

parts:
  Part1 = Arduino Nano (Rev3.0)
  ESP32_-_Back1 = ESP32 - CAM

nets:
  N1: Part1.D1/TX, ESP32_-_Back1.GPIO1_/_TX
  N2: Part1.D0/RX, ESP32_-_Back1.GPIO3_/_RX
  N3: Part1.RESET, Part1.GND
  N4: ESP32_-_Back1.GPIO0, ESP32_-_Back1.GND#12

custom parts:
  ESP32 - CAM: The ESP32-CAM has a very competitive small-size camera module that can operate independently as a minimum system with a footprint of only 27*40.5*4.5mm and a deep sleep current of up to 6mA.
